# Fritzing sketch Arduino Sketch - DHT22 (saved by Fritzing 1.0.1rc)
breadboards: 1

parts:
  元件1 = Arduino Uno (Rev3)
  DHT1 = DHT22 Humidity and Temperature Sensor

nets:
  N1: 元件1.D2, DHT1.DATA
  5V: 元件1.5V, DHT1.VDD
  GND: 元件1.GND, DHT1.GND
