# Fritzing sketch Arduino Sketch - 1602A I2C (saved by Fritzing 1.0.1rc)
breadboards: 1

parts:
  元件1 = Arduino Uno (Rev3)
  元件4 = LCD1602-I2C

nets:
  N1: 元件1.A4/SDA, 元件4.SDA
  N2: 元件1.A5/SCL, 元件4.SCL
  5V: 元件1.5V, 元件4.VCC
  GND: 元件1.GND, 元件4.GND

custom parts:
  LCD1602-I2C: A standard character display, usually with 2x16 characters. Comes in many colors with LCM1602 IIC attached.
