# Fritzing sketch Arduino Sketch - BMP390 (saved by Fritzing 1.0.1rc)
breadboards: 1

parts:
  元件1 = Arduino Uno (Rev3)
  元件4 = Adafruit BMP390 [part_number="Adafruit #4816"]

nets:
  N1: 元件1.A4/SDA, 元件4.SDI/SDA
  N2: 元件1.A5/SCL, 元件4.SCK/SCL
  5V: 元件1.5V, 元件4.VCC
  GND: 元件1.GND, 元件4.GND

custom parts:
  Adafruit BMP390: Bosch has been a leader in barometric pressure sensors, from the BMP085. BMP180, BMP280, BMP388... now we've got the next generation, the Adafruit BMP390 Precision Barometric Pressure and Altimeter Breakout. As you would expect, this sensor is similar to its earlier versions but even better. The BMP390 has better precision than ever, which makes it excellent for environmental sensing or as a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
