# Fritzing sketch Arduino Sketch - DHT22_SD (saved by Fritzing 1.0.1rc)
breadboards: 1

parts:
  元件1 = Arduino Uno (Rev3)
  RHT2 = Humidity and Temperature Sensor RHT03 [part_number=DHT22]
  microSD1 = MicroSD Card Module  # not connected

nets:
  N1: 元件1.D2, RHT2.Data-signal
  5V: 元件1.5V, RHT2.Vcc
  N2: 元件1.GND, RHT2.GND_2
