# Fritzing sketch Arduino Sketch - TSL2561 (saved by Fritzing 1.0.1rc)
breadboards: 1

parts:
  元件1 = Arduino Uno (Rev3)
  元件3 = Adafruit TSL2561 [part_number="Adafruit #439"]

nets:
  N1: 元件1.A4/SDA, 元件3.SDA
  N2: 元件1.A5/SCL, 元件3.SCL
  5V: 元件1.5V, 元件3.VIN
  GND: 元件1.GND, 元件3.GND

custom parts:
  Adafruit TSL2561: The TSL2561 luminosity sensor is an advanced digital light sensor, ideal for use in a wide range of light situations. Compared to low cost CdS cells, this sensor is more precise, allowing for exact lux calculations and can be configured for different gain/timing ranges to detect light ranges from up to 0.1 - 40,000+ Lux on the fly. The best part of this sensor is that it contains both infrared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
